# Fritzing sketch LedStripIR (saved by Fritzing 0.9.3b)

parts:
  R1 = Resistor [tolerance=±5% resistance=1k package=THT]
  Power_plug1 = Power plug
  Power_plug2 = Power plug
  IR1 = TSOP312.., 314.. [package=THT]
  Part1 = Arduino Nano (Rev3.0)
  Q3 = npn-Powertransistor [package="TO220 [THT]"]

nets:
  N1: R1.Pin_0, Q3.base
  N2: R1.Pin_1, Part1.D3
  GND: Power_plug1.GND, IR1.Vs, Part1.GND, Q3.collector
  VCC: Power_plug1.VCC, Power_plug2.VCC, Part1.VIN
  N3: Power_plug2.GND, Q3.emitter
  N4: IR1.GND, Part1.D6
  N5: IR1.Data, Part1.5V

notes:
  12v Iput
  LedStrip Output
  BD140
  1k
